# Fritzing sketch wordclock (saved by Fritzing 0.9.2b)
breadboards: 1

parts:
  Part1 = Arduino Nano (Rev3.0)
  RGB_SMD_LED1 = SMD RGB LED (WS2812) [package=5050]
  Part2 = Real Time Clock Module - DS1307 RTC Breakout Board
  RE1 = Rotary Encoder [package=THT]
  S1 = Pushbutton [package="[SMD]"]

nets:
  GND: Part1.GND, RGB_SMD_LED1.DOut, Part2.GND, RE1.EncoderPinC, S1.Pin_1, S1.Pin_2
  N1: Part1.D2, RE1.EncoderPinB
  N2: Part1.D3, RE1.EncoderPinA
  N3: Part1.D4, S1.Pin_3, S1.Pin_4
  N4: Part1.D8, RGB_SMD_LED1.DIn
  5V: Part1.5V, RGB_SMD_LED1.VCC, Part2.5V
  N5: Part1.A5, Part2.SCL
  N6: Part1.A4, Part2.SDA
